// Logisim project CPU.circ as structural Verilog: 3 circuits, main circuit RegisterBank
module RegisterBank (
  input  [15:0] DATA_IN,
  input  [2:0] READ_ADDR,
  input  READ_ENABLE,
  input  [2:0] WRITE_ADDR,
  input  WRITE_ENABLE,
  output [15:0] Data_Out
);

  wire clock_1_out, decoder_1_out0, decoder_1_out1, decoder_1_out2, decoder_1_out3, decoder_1_out4,
       decoder_1_out5, decoder_1_out6, decoder_1_out7, not_1_out;
  wire [15:0] controlled_buffer_1_out, Reg0_q, Reg1_q, Reg2_q, Reg3_q, Reg4_q, Reg5_q, Reg6_q, Reg7_q;

  Pull_Resistor pull_resistor_1 (.node(WRITE_ENABLE));
  Decoder #(.select(3), .disabled(0)) decoder_1 (
    .out0(decoder_1_out0), .out1(decoder_1_out1), .out2(decoder_1_out2), .out3(decoder_1_out3),
    .out4(decoder_1_out4), .out5(decoder_1_out5), .out6(decoder_1_out6), .out7(decoder_1_out7),
    .sel(WRITE_ADDR), .en(WRITE_ENABLE));
  Clock clock_1 (.out(clock_1_out));
  not not_1 (not_1_out, READ_ENABLE);
  assign controlled_buffer_1_out = not_1_out ? DATA_IN : 16'bz;  // Controlled_Buffer controlled_buffer_1
  Register #(.width(16)) Reg0 (
    .D(controlled_buffer_1_out), .en(decoder_1_out0), .Q(Reg0_q), .clk(clock_1_out));  // open: clr
  Register #(.width(16)) Reg1 (
    .D(controlled_buffer_1_out), .en(decoder_1_out1), .Q(Reg1_q), .clk(clock_1_out));  // open: clr
  Register #(.width(16)) Reg2 (
    .D(controlled_buffer_1_out), .en(decoder_1_out2), .Q(Reg2_q), .clk(clock_1_out));  // open: clr
  Register #(.width(16)) Reg3 (
    .D(controlled_buffer_1_out), .en(decoder_1_out3), .Q(Reg3_q), .clk(clock_1_out));  // open: clr
  Register #(.width(16)) Reg4 (
    .D(controlled_buffer_1_out), .en(decoder_1_out4), .Q(Reg4_q), .clk(clock_1_out));  // open: clr
  Register #(.width(16)) Reg5 (
    .D(controlled_buffer_1_out), .en(decoder_1_out5), .Q(Reg5_q), .clk(clock_1_out));  // open: clr
  Register #(.width(16)) Reg6 (
    .D(controlled_buffer_1_out), .en(decoder_1_out6), .Q(Reg6_q), .clk(clock_1_out));  // open: clr
  Register #(.width(16)) Reg7 (
    .D(controlled_buffer_1_out), .en(decoder_1_out7), .Q(Reg7_q), .clk(clock_1_out));  // open: clr
  assign controlled_buffer_1_out = Data_Out;  // Buffer buffer_1, 16 bits wide
  Pull_Resistor pull_resistor_2 (.node(READ_ENABLE));
  Multiplexer #(.select(3), .width(16)) multiplexer_1 (
    .in0(Reg0_q), .in1(Reg1_q), .in2(Reg2_q), .in3(Reg3_q), .in4(Reg4_q), .in5(Reg5_q), .in6(Reg6_q),
    .in7(Reg7_q), .out(Data_Out), .sel(READ_ADDR), .en(READ_ENABLE));

  // Notes on the sheet:
  //   READ_ADDR: pull=down
  //   WRITE_ADDR: pull=down
  //   DATA_IN: pull=down
endmodule

module ALU (
  input  [1:0] OPCODE_IN,
  input  READ_WRITE,
  input  [15:0] DATA_IN,
  input  ADDR,
  output [15:0] DATA_OUT,
  output REGA___REGB,
  output REGA___REGB_2,
  output REGA___REGB_3
);

  wire clock_1_out, decoder_1_out0, decoder_1_out1, not_1_out;
  wire [15:0] adder_1_out, controlled_buffer_1_out, nor_1_out, RegA_q, RegB_q, subtractor_1_out;

  assign controlled_buffer_1_out = READ_WRITE ? DATA_IN : 16'bz;  // Controlled_Buffer controlled_buffer_1
  Decoder #(.disabled(0)) decoder_1 (.out0(decoder_1_out0), .out1(decoder_1_out1), .sel(ADDR), .en(READ_WRITE));
  Register #(.width(16)) RegA (
    .D(controlled_buffer_1_out), .en(decoder_1_out0), .Q(RegA_q), .clk(clock_1_out));  // open: clr
  Clock clock_1 (.out(clock_1_out));
  Register #(.width(16)) RegB (
    .D(controlled_buffer_1_out), .en(decoder_1_out1), .Q(RegB_q), .clk(clock_1_out));  // open: clr
  Adder #(.width(16)) adder_1 (.a(RegA_q), .b(RegB_q), .out(adder_1_out));  // open: cin, cout
  Subtractor #(.width(16)) subtractor_1 (.a(RegA_q), .b(RegB_q), .out(subtractor_1_out));  // open: bin, bout
  assign nor_1_out = ~(RegA_q | RegB_q);  // NOR_Gate nor_1, 16 bits wide
  Comparator #(.width(16)) comparator_1 (
    .a(RegA_q), .b(RegB_q), .gt(REGA___REGB), .eq(REGA___REGB_2), .lt(REGA___REGB_3));
  not not_1 (not_1_out, READ_WRITE);
  Multiplexer #(.select(2), .width(16)) multiplexer_1 (
    .in1(adder_1_out), .in2(subtractor_1_out), .in3(nor_1_out), .out(DATA_OUT), .sel(OPCODE_IN),
    .en(not_1_out));  // open: in0

  // Notes on the sheet:
  //   REGA___REGB_2: pull=down
  //   REGA___REGB_3: pull=down
  //   REGA___REGB: pull=down
  //   DATA_IN: pull=down
endmodule

module CPU (
  input  [15:0] in_1,
  input  [15:0] in_2,
  input  in_3,
  input  in_4,
  output [15:0] out_5
);

  wire alu_1_rega___regb, alu_1_rega___regb_2, alu_1_rega___regb_3, ALU_R_W, ALU_REG_SELECT, CPU_R_W,
       not_1_out, REG_R_ENABLE, REG_W_ENABLE;
  wire [1:0] ALU_OP_SELECT;
  wire [2:0] REG_R_ADDR, REG_W_ADDR;
  wire [15:0] INSTRUCTION, registerbank_1_data_out;

  RegisterBank registerbank_1 (
    .DATA_IN(registerbank_1_data_out), .Data_Out(registerbank_1_data_out), .WRITE_ENABLE(REG_W_ENABLE),
    .READ_ENABLE(REG_R_ENABLE), .WRITE_ADDR(REG_W_ADDR), .READ_ADDR(REG_R_ADDR));
  ALU alu_1 (
    .DATA_IN(registerbank_1_data_out), .DATA_OUT(registerbank_1_data_out), .REGA___REGB(alu_1_rega___regb),
    .REGA___REGB_2(alu_1_rega___regb_2), .REGA___REGB_3(alu_1_rega___regb_3), .ADDR(ALU_REG_SELECT),
    .READ_WRITE(ALU_R_W), .OPCODE_IN(ALU_OP_SELECT));
  assign registerbank_1_data_out = CPU_R_W ? in_1 : 16'bz;  // Controlled_Buffer controlled_buffer_1
  not not_1 (not_1_out, CPU_R_W);
  assign out_5 = not_1_out ? registerbank_1_data_out : 16'bz;  // Controlled_Buffer controlled_buffer_2
  Register #(.width(16)) register_1 (.D(in_2), .en(in_3), .Q(INSTRUCTION), .clk(in_4));  // open: clr
  Decoder #(.select(3), .disabled(0), .enable("false")) decoder_1 (.sel(INSTRUCTION[15:13]));  // open: out0, out1, out2, out3, out4, out5, out6, out7
  // Probe on INSTRUCTION[15:13]

  // Other names for the same wires on the sheet: RegC[2:0] = INSTRUCTION[2:0]; RegB[2:0] = INSTRUCTION[5:3];
  //   RegA[2:0] = INSTRUCTION[12:10]; OPCODE[2:0] = INSTRUCTION[15:13]

  // Notes on the sheet:
  //   in_3: pull=down
  //   in_1: pull=down
  //   in_2: pull=down
  //   in_4: pull=down
  //   Registers
  //   ALU
  //   RRR
endmodule
